# Fritzing sketch meteo_schema (saved by Fritzing 0.9.3b)

parts:
  WeMos_D1_Mini1 = WeMos D1 Mini
  D1 = Schottky Diode [part_number=1N5817 package="Melf DO-213 AB [SMD]"]
  Součástka1 = GY-BMEP280 Barometric Pressure Sensor - Breakout
  TP1 = TP4056 [chip_label=TP4056 package="DIP (Dual Inline) [THT]"]
  U2 = LIPO-110mAh [package=lipo-110]
  Součástka2 = Solar Cell
  R1 = Resistor [tolerance=±5% resistance=100k package="2010 [SMD]"]
  M1 = RioRand LM2596
  Součástka3 = INA219 High Side DC Current Sensor Breakout [part_number=904]

nets:
  VCC: WeMos_D1_Mini1.3V3, Součástka1.VCC, Součástka1.CSB, Součástka1.SDO, Součástka3.VCC
  N1: WeMos_D1_Mini1.5V, TP1.pin3
  N2: WeMos_D1_Mini1.A0, R1.Pin_0
  N3: WeMos_D1_Mini1.D0, WeMos_D1_Mini1.RST
  N4: WeMos_D1_Mini1.D1, Součástka1.SCL, Součástka3.SCL
  N5: WeMos_D1_Mini1.D2, Součástka1.SDA, Součástka3.SDA
  GND: WeMos_D1_Mini1.G, Součástka1.GND, TP1.pin6, Součástka3.GND
  N6: D1.cathode, M1.Pin_1
  N7: D1.anode, Součástka3.VIN-
  N8: TP1.pin1, M1.Pin_3
  N9: TP1.pin2, Součástka2.-, M1.Pin_4
  N10: TP1.pin4, U2.+, R1.Pin_1
  N11: TP1.pin5, U2.-
  N12: Součástka2.+, Součástka3.VIN+

notes:
  6V 1W Solar panel
  18650 3400mAh battery 3.7V Li-ion
  GY-BME280-3.3
  100kΩ
  HW-613 MINI DCDC Buck Module, otput set to 5V
  V0+ : To batery charger
  IN+ : To solar panels next to Zener diode
  GND : GND
  INA219 for solar power monitoring
  TP4056 battery charger

custom parts:
  GY-BMEP280 Barometric Pressure Sensor - Breakout: The BME280 is a chip which was originally designed for the next generation of smartphones. It is made up of a very accurate pressure sensor and an associated temperature sensor which helps calibrate the pressure readings. And just for fun they threw in a pretty solid humidity sensor in there as well! So with an I2C connection you have access to enough weather data to make some pretty good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
  TP4056: A DIP stand-in part for whatever IC you want. With 6 pins on a 300mil dual inline package (DIP) footprint.
  INA219 High Side DC Current Sensor Breakout: This breakout board will solve all your power-monitoring problems. Instead of struggling with two multimeters, you can just use the handy INA219B chip on this breakout to both measure both the high side voltage and DC current draw over I2C with 1% precision. Most current-measuring devices such as our current panel meter are only good for low side measuring. That means that unless you want to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
